// Logisim project ArquiteturaDeComputadores.circ as structural Verilog
module Add1 (
  input  A,
  input  B,
  input  CARRY_IN,
  output S,
  output CARRY_OUT
);

  wire and_1_out, and_2_out, or_1_out, xor_1_out;

  xor xor_1 (xor_1_out, A, B);
  or or_1 (or_1_out, B, CARRY_IN);
  xor xor_2 (S, xor_1_out, CARRY_IN);
  and and_1 (and_1_out, B, CARRY_IN);
  and and_2 (and_2_out, or_1_out, A);
  or or_2 (CARRY_OUT, and_2_out, and_1_out);
endmodule
